// Logisim project BrianLinCPUhomework4.circ as structural Verilog: 3 circuits, main circuit singleRegister
module singleRegister (
  input  Reset,
  input  [15:0] In,
  output [15:0] Out
);

  wire clock_1_out, x1;

  Clock clock_1 (.out(clock_1_out));
  D_Flip_Flop d_ff_1 (.clk(clock_1_out), .D(In[0]), .Q(Out[0]), .reset(Reset));  // open: Qn, preset, en
  D_Flip_Flop d_ff_2 (.clk(clock_1_out), .D(In[1]), .Q(x1), .reset(Reset));  // open: Qn, preset, en
  D_Flip_Flop d_ff_3 (.clk(clock_1_out), .D(In[2]), .Q(Out[2]), .reset(Reset));  // open: Qn, preset, en
  D_Flip_Flop d_ff_4 (.clk(clock_1_out), .D(In[3]), .Q(Out[3]));  // open: Qn, preset, en, reset
  D_Flip_Flop d_ff_5 (.clk(clock_1_out), .D(In[4]), .Q(Out[4]), .reset(Reset));  // open: Qn, preset, en
  D_Flip_Flop d_ff_6 (.clk(clock_1_out), .D(In[5]), .Q(Out[5]), .reset(Reset));  // open: Qn, preset, en
  D_Flip_Flop d_ff_7 (.clk(clock_1_out), .D(In[6]), .Q(Out[6]), .reset(Reset));  // open: Qn, preset, en
  D_Flip_Flop d_ff_8 (.clk(clock_1_out), .D(In[7]), .Q(Out[7]));  // open: Qn, preset, en, reset
  D_Flip_Flop d_ff_9 (.clk(clock_1_out), .D(In[8]), .Q(Out[8]), .reset(Reset));  // open: Qn, preset, en
  D_Flip_Flop d_ff_10 (.clk(clock_1_out), .D(In[9]), .Q(Out[9]), .reset(Reset));  // open: Qn, preset, en
  D_Flip_Flop d_ff_11 (.clk(clock_1_out), .D(In[10]), .Q(Out[10]), .reset(Reset));  // open: Qn, preset, en
  D_Flip_Flop d_ff_12 (.clk(clock_1_out), .D(In[11]), .Q(Out[11]));  // open: Qn, preset, en, reset
  D_Flip_Flop d_ff_13 (.clk(clock_1_out), .D(In[12]), .Q(Out[12]), .reset(Reset));  // open: Qn, preset, en
  D_Flip_Flop d_ff_14 (.clk(clock_1_out), .D(In[13]), .Q(Out[13]), .reset(Reset));  // open: Qn, preset, en
  D_Flip_Flop d_ff_15 (.clk(clock_1_out), .D(In[14]), .Q(Out[14]), .reset(Reset));  // open: Qn, preset, en
  D_Flip_Flop d_ff_16 (.clk(clock_1_out), .D(In[15]), .Q(Out[15]));  // open: Qn, preset, en, reset

  assign Out[1] = Out[2];

  // Other names for the same wires on the sheet: _0 = In[0]; _1 = In[1]; _2 = In[2]; _3 = In[3]; _4 = In[4];
  //   _5 = In[5]; _6 = In[6]; _7 = In[7]; _8 = In[8]; _9 = In[9]; _10 = In[10]; _11 = In[11]; _12 = In[12];
  //   _13 = In[13]; _14 = In[14]; _15 = In[15]; x0 = Out[0]; x2 = Out[2]; x3 = Out[3]; x4 = Out[4]; x5 = Out[5];
  //   x6 = Out[6]; x7 = Out[7]; x8 = Out[8]; x9 = Out[9]; x10 = Out[10]; x11 = Out[11]; x12 = Out[12]; x13 = Out[13];
  //   x14 = Out[14]; x15 = Out[15]
endmodule

module registerFile (
  input  Reset,
  input  RegWriteEnable,
  input  [3:0] WriteReg,
  input  [3:0] ReadReg1,
  input  [15:0] WriteData,
  output [15:0] ReadData1
);

  wire [15:0] A0, A1, A2, A3, A4, A5, A6, A7, A8, A9, A10, A11, A12, A13, A14, A15, W0, W1, W2, W3, W4, W5,
       W6, W7, W8, W9, W10, W11, W12, W13, W14, W15;

  Demultiplexer #(.select(4), .width(16)) demultiplexer_1 (
    .out0(W0), .out1(W1), .out2(W2), .out3(W3), .out4(W4), .out5(W5), .out6(W6), .out7(W7), .out8(W8),
    .out9(W9), .out10(W10), .out11(W11), .out12(W12), .out13(W13), .out14(W14), .out15(W15), .in(WriteData),
    .sel(WriteReg), .en(RegWriteEnable));
  singleRegister R0 (.In({16{1'b0}}), .Reset(Reset), .Out(A0));
  singleRegister R4 (.In(W4), .Reset(Reset), .Out(A4));
  singleRegister R8 (.In(W8), .Reset(Reset), .Out(A8));
  singleRegister R12 (.In(W12), .Reset(Reset), .Out(A12));
  singleRegister R1 (.In(W1), .Reset(Reset), .Out(A1));
  singleRegister R5 (.In(W5), .Reset(Reset), .Out(A5));
  singleRegister R9 (.In(W9), .Reset(Reset), .Out(A9));
  singleRegister R13 (.In(W13), .Reset(Reset), .Out(A13));
  singleRegister R2 (.In(W2), .Reset(Reset), .Out(A2));
  singleRegister R6 (.In(W6), .Reset(Reset), .Out(A6));
  singleRegister R10 (.In(W10), .Reset(Reset), .Out(A10));
  singleRegister R14 (.In(W14), .Reset(Reset), .Out(A14));
  singleRegister R3 (.In(W3), .Reset(Reset), .Out(A3));
  singleRegister R7 (.In(W7), .Reset(Reset), .Out(A7));
  singleRegister R11 (.In(W11), .Reset(Reset), .Out(A11));
  singleRegister R15 (.In(W15), .Reset(Reset), .Out(A15));
  Multiplexer #(.select(4), .width(16), .enable("false")) multiplexer_1 (
    .in0(A0), .in1(A1), .in2(A2), .in3(A3), .in4(A4), .in5(A5), .in6(A6), .in7(A7), .in8(A8), .in9(A9),
    .in10(A10), .in11(A11), .in12(A12), .in13(A13), .in14(A14), .in15(A15), .out(ReadData1), .sel(ReadReg1));

  // Other names for the same wires on the sheet: aIn[3:0] = ReadReg1; RWE = RegWriteEnable;
  //   whichWrite[3:0] = WriteReg

  // Notes on the sheet:
  //   A-Out
endmodule

module ALU (
  input  [3:0] Opcode,
  input  [15:0] InputData1,
  output [15:0] OutputData
);
endmodule
