// Logisim project register.circ as structural Verilog: 1 circuit, main circuit main
module main (
  input  Reset,
  input  [15:0] in_2
);

  wire clock_1_out, x0, x1, x2, x3, x4, x5, x6, x7, x8, x9, x10, x11, x12, x13, x14, x15;

  Clock clock_1 (.out(clock_1_out));
  D_Flip_Flop d_ff_1 (.clk(clock_1_out), .D(in_2[0]), .Q(x0), .reset(Reset));  // open: Qn, preset, en
  D_Flip_Flop d_ff_2 (.clk(clock_1_out), .D(in_2[1]), .Q(x1), .reset(Reset));  // open: Qn, preset, en
  D_Flip_Flop d_ff_3 (.clk(clock_1_out), .D(in_2[2]), .Q(x2), .reset(Reset));  // open: Qn, preset, en
  D_Flip_Flop d_ff_4 (.clk(clock_1_out), .D(in_2[3]), .Q(x3));  // open: Qn, preset, en, reset
  D_Flip_Flop d_ff_5 (.clk(clock_1_out), .D(in_2[4]), .Q(x4), .reset(Reset));  // open: Qn, preset, en
  D_Flip_Flop d_ff_6 (.clk(clock_1_out), .D(in_2[5]), .Q(x5), .reset(Reset));  // open: Qn, preset, en
  D_Flip_Flop d_ff_7 (.clk(clock_1_out), .D(in_2[6]), .Q(x6), .reset(Reset));  // open: Qn, preset, en
  D_Flip_Flop d_ff_8 (.clk(clock_1_out), .D(in_2[7]), .Q(x7));  // open: Qn, preset, en, reset
  D_Flip_Flop d_ff_9 (.clk(clock_1_out), .D(in_2[8]), .Q(x8), .reset(Reset));  // open: Qn, preset, en
  D_Flip_Flop d_ff_10 (.clk(clock_1_out), .D(in_2[9]), .Q(x9), .reset(Reset));  // open: Qn, preset, en
  D_Flip_Flop d_ff_11 (.clk(clock_1_out), .D(in_2[10]), .Q(x10), .reset(Reset));  // open: Qn, preset, en
  D_Flip_Flop d_ff_12 (.clk(clock_1_out), .D(in_2[11]), .Q(x11));  // open: Qn, preset, en, reset
  D_Flip_Flop d_ff_13 (.clk(clock_1_out), .D(in_2[12]), .Q(x12), .reset(Reset));  // open: Qn, preset, en
  D_Flip_Flop d_ff_14 (.clk(clock_1_out), .D(in_2[13]), .Q(x13), .reset(Reset));  // open: Qn, preset, en
  D_Flip_Flop d_ff_15 (.clk(clock_1_out), .D(in_2[14]), .Q(x14), .reset(Reset));  // open: Qn, preset, en
  D_Flip_Flop d_ff_16 (.clk(clock_1_out), .D(in_2[15]), .Q(x15));  // open: Qn, preset, en, reset

  // Other names for the same wires on the sheet: _0 = in_2[0]; _1 = in_2[1]; _2 = in_2[2]; _3 = in_2[3]; _4 = in_2[4];
  //   _5 = in_2[5]; _6 = in_2[6]; _7 = in_2[7]; _8 = in_2[8]; _9 = in_2[9]; _10 = in_2[10]; _11 = in_2[11];
  //   _12 = in_2[12]; _13 = in_2[13]; _14 = in_2[14]; _15 = in_2[15]
endmodule
