// Logisim project adder.circ as structural Verilog: 2 circuits, main circuit actualMain
module main (
  input  A,
  input  B,
  input  carryIn,
  output Sum,
  output carryOut
);

  wire and_1_out, and_2_out, and_3_out, and_4_out, and_5_out, and_6_out, and_7_out, not_1_out, not_2_out,
       not_3_out;

  not not_1 (not_1_out, A);
  not not_2 (not_2_out, B);
  not not_3 (not_3_out, carryIn);
  and and_1 (and_1_out, not_1_out, not_2_out, carryIn);
  and and_2 (and_2_out, not_1_out, B, not_3_out);
  and and_3 (and_3_out, A, not_2_out, not_3_out);
  and and_4 (and_4_out, A, B, carryIn);
  and and_5 (and_5_out, B, carryIn);
  and and_6 (and_6_out, B, A);
  and and_7 (and_7_out, carryIn, A);
  or or_1 (Sum, and_1_out, and_2_out, and_3_out, and_4_out);
  or or_2 (carryOut, and_5_out, and_6_out, and_7_out);
endmodule

module actualMain (
  input  A0,
  input  B0,
  input  carryIn,
  input  A1,
  input  B1,
  input  A2,
  input  B2,
  input  A3,
  input  B3,
  input  A4,
  input  B4,
  input  A5,
  input  B5,
  input  A6,
  input  B6,
  input  A7,
  input  B7,
  input  in_18,
  input  in_19,
  input  in_20,
  input  in_21,
  input  in_22,
  input  in_23,
  input  in_24,
  input  in_25,
  input  in_26,
  input  in_27,
  output Sum0,
  output Sum1,
  output Sum2,
  output out_31,
  output out_32,
  output out_33,
  output out_34,
  output out_35
);

  wire main_1_carryout, main_2_carryout, main_3_carryout, main_4_carryout, main_5_carryout, main_6_carryout,
       main_7_carryout;

  main main_1 (.A(A0), .B(B0), .carryIn(carryIn), .Sum(Sum0), .carryOut(main_1_carryout));
  main main_2 (.A(A1), .B(B1), .carryIn(main_1_carryout), .Sum(Sum1), .carryOut(main_2_carryout));
  main main_3 (.A(A2), .B(B2), .carryIn(main_2_carryout), .Sum(Sum2), .carryOut(main_3_carryout));
  main main_4 (.A(A3), .B(B3), .carryIn(main_3_carryout), .Sum(out_31), .carryOut(main_4_carryout));
  main main_5 (.A(A4), .B(A4), .carryIn(main_4_carryout), .Sum(out_32), .carryOut(main_5_carryout));
  main main_6 (.A(A5), .B(B5), .carryIn(main_5_carryout), .Sum(out_33), .carryOut(main_6_carryout));
  main main_7 (.A(A6), .B(B6), .carryIn(main_6_carryout), .Sum(out_34), .carryOut(main_7_carryout));
  main main_8 (.A(A7), .B(B7), .carryIn(main_7_carryout), .Sum(out_35));  // open: carryOut
  main main_9 ();  // open: A, B, carryIn, Sum, carryOut
  main main_10 ();  // open: A, B, carryIn, Sum, carryOut
  main main_11 ();  // open: A, B, carryIn, Sum, carryOut
  main main_12 ();  // open: A, B, carryIn, Sum, carryOut
  main main_13 ();  // open: A, B, carryIn, Sum, carryOut

  assign B4 = A4;
endmodule
