// Logisim project question6.circ as structural Verilog: 1 circuit, main circuit main
module main (
  input  in1,
  input  in2
);

  wire and_1_out, and_2_out, and_3_out, D0_Q0_q, D1_Q1_q, not_1_out, not_2_out, or_1_out, or_2_out;

  not not_1 (not_1_out, in1);
  not not_2 (not_2_out, in2);
  and and_1 (and_1_out, not_2_out, in2);
  and and_2 (and_2_out, in1, not_1_out);
  or or_1 (or_1_out, and_1_out, and_2_out);
  and and_3 (and_3_out, or_1_out, or_2_out);
  or or_2 (or_2_out, D1_Q1_q, D0_Q0_q);
  D_Flip_Flop D1_Q1 (.D(and_3_out), .Q(D1_Q1_q));  // open: clk, Qn, preset, en, reset
  D_Flip_Flop D0_Q0 (.Q(D0_Q0_q));  // open: clk, D, Qn, preset, en, reset
endmodule
